// Digital circuit ALU.dig as structural Verilog
module ALU (
  input  [15:0] b,
  input  [15:0] a,
  input  [3:0] s,
  output overflow,
  output zero,
  output [15:0] r
);

  wire alu0_co, alu1_co, alu2_co, alu3_co, alu4_co, alu5_co, alu6_co, alu7_co, alu8_co, alu9_co, alu10_co,
       alu11_co, alu12_co, alu13_co, alu14_co, alu15_p8;

  ALU1 alu0 (.a(a[0]), .b(b[0]), .less(alu15_p8), .ci(s[2]), .s(s), .r(r[0]), .co(alu0_co));
  ALU1 alu1 (.a(a[1]), .b(b[1]), .less(1'b0), .ci(alu0_co), .s(s), .r(r[1]), .co(alu1_co));
  ALU1 alu2 (.a(a[2]), .b(b[2]), .less(1'b0), .ci(alu1_co), .s(s), .r(r[2]), .co(alu2_co));
  ALU1 alu3 (.a(a[3]), .b(b[3]), .less(1'b0), .ci(alu2_co), .s(s), .r(r[3]), .co(alu3_co));
  ALU1 alu4 (.a(a[4]), .b(b[4]), .less(1'b0), .ci(alu3_co), .s(s), .r(r[4]), .co(alu4_co));
  ALU1 alu5 (.a(a[5]), .b(b[5]), .less(1'b0), .ci(alu4_co), .s(s), .r(r[5]), .co(alu5_co));
  ALU1 alu6 (.a(a[6]), .b(b[6]), .less(1'b0), .ci(alu5_co), .s(s), .r(r[6]), .co(alu6_co));
  ALU1 alu7 (.a(a[7]), .b(b[7]), .less(1'b0), .ci(alu6_co), .s(s), .r(r[7]), .co(alu7_co));
  ALU1 alu8 (.a(a[8]), .b(b[8]), .less(1'b0), .ci(alu7_co), .s(s), .r(r[8]), .co(alu8_co));
  ALU1 alu9 (.a(a[9]), .b(b[9]), .less(1'b0), .ci(alu8_co), .s(s), .r(r[9]), .co(alu9_co));
  ALU1 alu10 (.a(a[10]), .b(b[10]), .less(1'b0), .ci(alu9_co), .s(s), .r(r[10]), .co(alu10_co));
  ALU1 alu11 (.a(a[11]), .b(b[11]), .less(1'b0), .ci(alu10_co), .s(s), .r(r[11]), .co(alu11_co));
  ALU1 alu12 (.a(a[12]), .b(b[12]), .less(1'b0), .ci(alu11_co), .s(s), .r(r[12]), .co(alu12_co));
  ALU1 alu13 (.a(a[13]), .b(b[13]), .less(1'b0), .ci(alu12_co), .s(s), .r(r[13]), .co(alu13_co));
  ALU1 alu14 (.a(a[14]), .b(b[14]), .less(1'b0), .ci(alu13_co), .s(s), .r(r[14]), .co(alu14_co));
  // ALUmsb alu15: pin names not known; wires that end beside it: a[15], b[15], 1'b0, alu14_co, s, r[15], overflow, alu15_p8
  nor nor_1 (zero, r[0], r[1], r[2], r[3], r[4], r[5], r[6], r[7], r[8], r[9], r[10], r[11], r[12], r[13], r[14], r[15]);

  // Notes on the sheet:
  //   s[2]
  //   set
  //   co0
  //   co1
  //   co2
  //   co3
  //   co4
  //   co5
  //   co6
  //   co7
  //   co8
  //   co9
  //   co10
  //   co11
  //   co12
  //   co13
  //   co14
endmodule
