// Digital circuit BranchControl.dig as structural Verilog
module BranchControl (
  input  BEQ,
  input  BNE,
  input  Zero,
  output Taken
);

  wire and_1_out, and_2_out;

  and and_1 (and_1_out, BEQ, Zero);
  and and_2 (and_2_out, BNE, ~Zero);  // And
  or or_1 (Taken, and_1_out, and_2_out);

  // Notes on the sheet:
  //   BeqTaken
  //   BneTaken
endmodule
