// Digital circuit CPU.dig as structural Verilog
module CPU (
  input  in_1
);

  wire alu_2_zero, and_1_out, maincontrol_1_alusrc, maincontrol_1_bne, maincontrol_1_branch,
       maincontrol_1_memread, maincontrol_1_memtoreg, maincontrol_1_memwrite, maincontrol_1_regdistr,
       maincontrol_1_regwrite, multiplexer_3_out, not_1_out, or_1_out;
  wire [1:0] multiplexer_1_out;
  wire [3:0] maincontrol_1_aluop;
  wire [15:0] alu_1_r, alu_2_r, alu_3_r, counter_q, instr_d, multiplexer_2_out, multiplexer_4_out,
       ramdualport_1_d, reg_file_1_p4, reg_file_1_p6, reg_file_1_p7, shift_left_1_1_out, sign_extend_1__16;

  D_FF #(.Bits(16)) counter (.D(multiplexer_4_out), .C(~in_1), .Q(counter_q));  // open: nQ
  ROM #(.AddrBits(16), .Bits(16)) instr (.A(counter_q), .sel(1'b1), .D(instr_d));
  Multiplexer #(.Bits(2)) multiplexer_1 (
    .sel(maincontrol_1_regdistr), .in_0(instr_d[9:8]), .in_1(instr_d[7:6]), .out(multiplexer_1_out));
  ALU alu_1 (.r(alu_1_r), .a(counter_q), .b(16'h2), .s(4'b0010));  // open: zero, overflow
  MainControl maincontrol_1 (
    .op(instr_d[15:12]), .RegDistr(maincontrol_1_regdistr), .Branch(maincontrol_1_branch),
    .BNE(maincontrol_1_bne), .MemRead(maincontrol_1_memread), .MemToReg(maincontrol_1_memtoreg),
    .ALUOp(maincontrol_1_aluop), .MemWrite(maincontrol_1_memwrite), .ALUSrc(maincontrol_1_alusrc),
    .RegWrite(maincontrol_1_regwrite));
  // reg_file reg_file_1: pin names not known; wires that end beside it: instr_d[11:10], instr_d[9:8], multiplexer_1_out, reg_file_1_p4, maincontrol_1_regwrite, reg_file_1_p6, reg_file_1_p7
  sign_extend sign_extend_1 (._8(instr_d[7:0]), ._16(sign_extend_1__16));
  Multiplexer #(.Bits(16)) multiplexer_2 (
    .sel(maincontrol_1_alusrc), .in_0(reg_file_1_p7), .in_1(sign_extend_1__16), .out(multiplexer_2_out));
  shift_left_1 shift_left_1_1 (.in(sign_extend_1__16), .out(shift_left_1_1_out));
  ALU alu_2 (
    .zero(alu_2_zero), .r(alu_2_r), .a(reg_file_1_p6), .b(multiplexer_2_out), .s(maincontrol_1_aluop));  // open: overflow
  ALU alu_3 (.r(alu_3_r), .a(alu_1_r), .b(shift_left_1_1_out), .s(4'b0010));  // open: zero, overflow
  not not_1 (not_1_out, alu_2_zero);
  and and_1 (and_1_out, maincontrol_1_branch, multiplexer_3_out);
  Multiplexer multiplexer_3 (.sel(maincontrol_1_bne), .in_0(alu_2_zero), .in_1(not_1_out), .out(multiplexer_3_out));
  or or_1 (or_1_out, maincontrol_1_memwrite, maincontrol_1_memread);
  Multiplexer #(.Bits(16)) multiplexer_4 (.sel(and_1_out), .in_0(alu_1_r), .in_1(alu_3_r), .out(multiplexer_4_out));
  RAMDualPort #(.AddrBits(16), .Bits(16)) ramdualport_1 (
    .A(alu_2_r), .Din(reg_file_1_p7), .str(maincontrol_1_memwrite), .C(or_1_out), .ld(maincontrol_1_memread),
    .D(ramdualport_1_d));
  Multiplexer #(.Bits(16)) multiplexer_5 (
    .sel(maincontrol_1_memtoreg), .in_0(alu_2_r), .in_1(ramdualport_1_d), .out(reg_file_1_p4));
endmodule
