// Digital circuit reg_fwd_sel.dig as structural Verilog
module reg_fwd_sel (
  input  [1:0] WR,
  input  [1:0] IR,
  input  WE,
  output FWD
);

  wire nor_1_out;
  wire [1:0] xor_1_out;

  assign xor_1_out = IR ^ WR;  // XOr xor_1, 2 bits wide
  nor nor_1 (nor_1_out, xor_1_out[0], xor_1_out[1]);
  and and_1 (FWD, nor_1_out, WE);
endmodule
